// Logisim project computer.circ as structural Verilog: 10 circuits, main circuit main
module main (
  input  reset
);

  wire instructiondecoder_1_fu_select_alu_or_shifter, instructiondecoder_1_ram_enable_read,
       instructiondecoder_1_ram_enable_write, instructiondecoder_1_rf_enable_write, pc_clock_out;
  wire [1:0] instructiondecoder_1_fu_select_shifter, instructiondecoder_1_rf_address_output_a,
       instructiondecoder_1_rf_address_output_b, instructiondecoder_1_rf_address_write;
  wire [3:0] instructiondecoder_1_fu_select_alu;
  wire [7:0] functionunit_1_output_fu, programcounter_1_instruction_pointer, registerfile_1_output_a,
       registerfile_1_output_b;
  wire [11:0] Instruction_Memory_data;

  Clock pc_clock (.out(pc_clock_out));
  ProgramCounter programcounter_1 (
    .reset(reset), .increment(pc_clock_out), .Instruction_pointer(programcounter_1_instruction_pointer));
  ROM #(.dataWidth(12)) Instruction_Memory (
    .addr(programcounter_1_instruction_pointer), .data(Instruction_Memory_data));
  InstructionDecoder instructiondecoder_1 (
    .Instruction(Instruction_Memory_data[1:0]), .Input_variable(Instruction_Memory_data[9:2]),
    .Input_register(Instruction_Memory_data[11:10]), .RF_enable_write(instructiondecoder_1_rf_enable_write),
    .RF_address_write(instructiondecoder_1_rf_address_write),
    .RF_address_output_A(instructiondecoder_1_rf_address_output_a),
    .RF_address_output_B(instructiondecoder_1_rf_address_output_b),
    .FU_select_alu(instructiondecoder_1_fu_select_alu),
    .FU_select_shifter(instructiondecoder_1_fu_select_shifter),
    .FU_select_alu_or_shifter(instructiondecoder_1_fu_select_alu_or_shifter),
    .RAM_enable_write(instructiondecoder_1_ram_enable_write),
    .RAM_enable_read(instructiondecoder_1_ram_enable_read));
  RegisterFile registerfile_1 (
    .Input_RF(functionunit_1_output_fu), .enable_write(instructiondecoder_1_rf_enable_write),
    .address_write(instructiondecoder_1_rf_address_write),
    .address_output_A(instructiondecoder_1_rf_address_output_a),
    .address_output_B(instructiondecoder_1_rf_address_output_b), .Output_A(registerfile_1_output_a),
    .Output_B(registerfile_1_output_b));
  FunctionUnit functionunit_1 (
    .Input_A(registerfile_1_output_a), .Input_B(registerfile_1_output_b),
    .select_alu(instructiondecoder_1_fu_select_alu), .select_shifter(instructiondecoder_1_fu_select_shifter),
    .select_alu_or_shifter(instructiondecoder_1_fu_select_alu_or_shifter),
    .Output_FU(functionunit_1_output_fu));  // open: overflow
  RAM #(.trigger("high")) Data_Memory (
    .addr(registerfile_1_output_a), .we(instructiondecoder_1_ram_enable_write),
    .oe(instructiondecoder_1_ram_enable_read), .din(registerfile_1_output_b));  // open: dout
endmodule

module ram_perso (
  input  [7:0] address,
  input  write_enable,
  input  [7:0] input_word,
  input  in_4,
  output [7:0] output_word
);

  wire clock_1_out, not_1_out;
  wire [7:0] address_register_q, input_register_q, ram_1_dout;

  Clock clock_1 (.out(clock_1_out));
  Register address_register (.D(address), .en(in_4), .clk(clock_1_out), .Q(address_register_q));  // open: clr
  Register input_register (.D(input_word), .en(in_4), .clk(clock_1_out), .Q(input_register_q));  // open: clr
  Register output_register (.D(ram_1_dout), .en(in_4), .clk(clock_1_out), .Q(output_word));  // open: clr
  not not_1 (not_1_out, write_enable);
  RAM ram_1 (
    .addr(address_register_q), .we(write_enable), .oe(not_1_out), .clk(clock_1_out), .din(input_register_q),
    .dout(ram_1_dout));
endmodule

module ALU_AC (
  input  C_in,
  input  [1:0] S,
  input  [7:0] A,
  input  [7:0] B,
  output [7:0] G,
  output C_out
);

  wire and_1_out, and_2_out, and_3_out, and_4_out, and_5_out, and_6_out, and_7_out, and_8_out, and_9_out,
       and_10_out, and_11_out, and_12_out, and_13_out, and_14_out, and_15_out, and_16_out, not_1_out,
       not_2_out, not_3_out, not_4_out, not_5_out, not_6_out, not_7_out, not_8_out;
  wire [7:0] or_1_out;

  not not_1 (not_1_out, B[0]);
  not not_2 (not_2_out, B[1]);
  not not_3 (not_3_out, B[2]);
  not not_4 (not_4_out, B[3]);
  not not_5 (not_5_out, B[4]);
  not not_6 (not_6_out, B[5]);
  not not_7 (not_7_out, B[6]);
  not not_8 (not_8_out, B[7]);
  and and_1 (and_1_out, B[0], S[0]);
  and and_2 (and_2_out, not_1_out, S[1]);
  and and_3 (and_3_out, B[1], S[0]);
  and and_4 (and_4_out, not_2_out, S[1]);
  and and_5 (and_5_out, B[2], S[0]);
  and and_6 (and_6_out, not_3_out, S[1]);
  and and_7 (and_7_out, B[3], S[0]);
  and and_8 (and_8_out, not_4_out, S[1]);
  and and_9 (and_9_out, B[4], S[0]);
  and and_10 (and_10_out, not_5_out, S[1]);
  and and_11 (and_11_out, B[5], S[0]);
  and and_12 (and_12_out, not_6_out, S[1]);
  and and_13 (and_13_out, B[6], S[0]);
  and and_14 (and_14_out, not_7_out, S[1]);
  and and_15 (and_15_out, B[7], S[0]);
  and and_16 (and_16_out, not_8_out, S[1]);
  or or_1 (or_1_out[0], and_1_out, and_2_out);
  or or_2 (or_1_out[1], and_3_out, and_4_out);
  or or_3 (or_1_out[2], and_5_out, and_6_out);
  or or_4 (or_1_out[3], and_7_out, and_8_out);
  or or_5 (or_1_out[4], and_9_out, and_10_out);
  or or_6 (or_1_out[5], and_11_out, and_12_out);
  or or_7 (or_1_out[6], and_13_out, and_14_out);
  or or_8 (or_1_out[7], and_15_out, and_16_out);
  Adder adder_1 (.a(A), .b(or_1_out), .out(G), .cin(C_in), .cout(C_out));
endmodule

module ALU_LC (
  input  [1:0] S,
  input  [7:0] A,
  input  [7:0] B,
  output [7:0] G
);

  wire [7:0] and_1_out, not_1_out, or_1_out, xor_1_out;

  assign and_1_out = A & B;  // AND_Gate and_1, 8 bits wide
  assign or_1_out = A | B;  // OR_Gate or_1, 8 bits wide
  assign xor_1_out = A ^ B;  // XOR_Gate xor_1, 8 bits wide
  assign not_1_out = ~A;  // NOT_Gate not_1, 8 bits wide
  Multiplexer #(.select(2), .width(8)) multiplexer_1 (
    .in0(and_1_out), .in1(or_1_out), .in2(xor_1_out), .in3(not_1_out), .out(G), .sel(S));
endmodule

module ALU (
  input  C_in,
  input  [2:0] S,
  input  [7:0] A,
  input  [7:0] B,
  output C_overflow,
  output [7:0] G
);

  wire [7:0] alu_ac_1_g, alu_lc_1_g;

  ALU_AC alu_ac_1 (.C_in(C_in), .S(S[1:0]), .A(A), .B(B), .G(alu_ac_1_g), .C_out(C_overflow));
  ALU_LC alu_lc_1 (.S(S[1:0]), .A(A), .B(B), .G(alu_lc_1_g));
  Multiplexer #(.width(8)) multiplexer_1 (.in0(alu_ac_1_g), .in1(alu_lc_1_g), .out(G), .sel(S[2]));
endmodule

module Basic_Shifter (
  input  [7:0] A,
  input  Input_Left,
  input  Input_Right,
  input  [1:0] S,
  output [7:0] G
);

  wire undriven, undriven_2, undriven_3, undriven_4, undriven_5, undriven_6, undriven_7, undriven_8;

  // NoConnect on undriven
  Multiplexer #(.select(2)) multiplexer_1 (
    .in0(A[7]), .in1(Input_Right), .in2(A[6]), .in3(undriven), .out(G[7]), .sel(S));
  // NoConnect on undriven_2
  Multiplexer #(.select(2)) multiplexer_2 (.in0(A[6]), .in1(A[7]), .in2(A[5]), .in3(undriven_2), .out(G[6]), .sel(S));
  // NoConnect on undriven_3
  Multiplexer #(.select(2)) multiplexer_3 (.in0(A[5]), .in1(A[6]), .in2(A[4]), .in3(undriven_3), .out(G[5]), .sel(S));
  // NoConnect on undriven_4
  Multiplexer #(.select(2)) multiplexer_4 (.in0(A[4]), .in1(A[5]), .in2(A[3]), .in3(undriven_4), .out(G[4]), .sel(S));
  // NoConnect on undriven_5
  Multiplexer #(.select(2)) multiplexer_5 (.in0(A[3]), .in1(A[4]), .in2(A[2]), .in3(undriven_5), .out(G[3]), .sel(S));
  // NoConnect on undriven_6
  Multiplexer #(.select(2)) multiplexer_6 (.in0(A[2]), .in1(A[3]), .in2(A[1]), .in3(undriven_6), .out(G[2]), .sel(S));
  // NoConnect on undriven_7
  Multiplexer #(.select(2)) multiplexer_7 (.in0(A[1]), .in1(A[2]), .in2(A[0]), .in3(undriven_7), .out(G[1]), .sel(S));
  // NoConnect on undriven_8
  Multiplexer #(.select(2)) multiplexer_8 (
    .in0(A[0]), .in1(A[1]), .in2(Input_Left), .in3(undriven_8), .out(G[0]), .sel(S));
endmodule

module ProgramCounter (
  input  reset,
  input  increment,
  output [7:0] Instruction_pointer
);

  wire multiplexer_2_out;
  wire [7:0] counter_register_q, multiplexer_1_out;

  Multiplexer #(.width(8)) multiplexer_1 (
    .in0(Instruction_pointer), .in1({8{1'b0}}), .out(multiplexer_1_out), .sel(reset));
  Register counter_register (
    .D(multiplexer_1_out), .en(multiplexer_2_out), .clk(multiplexer_2_out), .Q(counter_register_q));  // open: clr
  Multiplexer multiplexer_2 (.in0(increment), .in1(reset), .out(multiplexer_2_out), .sel(reset));
  Adder adder_1 (.a(counter_register_q), .b(8'h1), .out(Instruction_pointer));  // open: cin, cout
endmodule

module InstructionDecoder (
  input  [1:0] Instruction,
  input  [7:0] Input_variable,
  input  [1:0] Input_register,
  output RF_enable_write,
  output [1:0] RF_address_write,
  output [1:0] RF_address_output_A,
  output [1:0] RF_address_output_B,
  output [3:0] FU_select_alu,
  output [1:0] FU_select_shifter,
  output FU_select_alu_or_shifter,
  output RAM_enable_write,
  output RAM_enable_read
);


  // Notes on the sheet:
  //   LOAD
  //   ADD
  //   STORE
endmodule

module FunctionUnit (
  input  [7:0] Input_A,
  input  [7:0] Input_B,
  input  [3:0] select_alu,
  input  [1:0] select_shifter,
  input  select_alu_or_shifter,
  output overflow,
  output [7:0] Output_FU
);

  wire [7:0] alu_1_g, basic_shifter_1_g;

  ALU alu_1 (.C_in(select_alu[0]), .S(select_alu[3:1]), .A(Input_A), .B(Input_B), .C_overflow(overflow), .G(alu_1_g));
  Basic_Shifter basic_shifter_1 (
    .A(Input_B), .Input_Left(1'b0), .Input_Right(1'b0), .S(select_shifter), .G(basic_shifter_1_g));
  Multiplexer #(.width(8)) multiplexer_1 (
    .in0(alu_1_g), .in1(basic_shifter_1_g), .out(Output_FU), .sel(select_alu_or_shifter));
endmodule

module RegisterFile (
  input  [7:0] Input_RF,
  input  enable_write,
  input  [1:0] address_write,
  input  [1:0] address_output_A,
  input  [1:0] address_output_B,
  output [7:0] Output_A,
  output [7:0] Output_B
);

  wire decoder_1_out0, decoder_1_out1, decoder_1_out2, decoder_1_out3;
  wire [7:0] registre_0_q, registre_1_q, registre_2_q, registre_3_q;

  Decoder #(.select(2)) decoder_1 (
    .out0(decoder_1_out0), .out1(decoder_1_out1), .out2(decoder_1_out2), .out3(decoder_1_out3),
    .sel(address_write), .en(enable_write));
  Register #(.trigger("high")) registre_0 (
    .D(Input_RF), .en(decoder_1_out0), .clk(decoder_1_out0), .Q(registre_0_q));  // open: clr
  Register #(.trigger("high")) registre_1 (
    .D(Input_RF), .en(decoder_1_out1), .clk(decoder_1_out1), .Q(registre_1_q));  // open: clr
  Register #(.trigger("high")) registre_2 (
    .D(Input_RF), .en(decoder_1_out2), .clk(decoder_1_out2), .Q(registre_2_q));  // open: clr
  Register #(.trigger("high")) registre_3 (
    .D(Input_RF), .en(decoder_1_out3), .clk(decoder_1_out3), .Q(registre_3_q));  // open: clr
  Multiplexer #(.select(2), .width(8)) multiplexer_1 (
    .in0(registre_0_q), .in1(registre_1_q), .in2(registre_2_q), .in3(registre_3_q), .out(Output_A),
    .sel(address_output_A));
  Multiplexer #(.select(2), .width(8)) multiplexer_2 (
    .in0(registre_0_q), .in1(registre_1_q), .in2(registre_2_q), .in3(registre_3_q), .out(Output_B),
    .sel(address_output_B));
endmodule
